# Fritzing sketch mcp23017_chain_master (saved by Fritzing 0.9.3b)
breadboards: 5

parts:
  R1 = Resistor [tolerance=±5% resistance=10k package=THT]
  R2 = Resistor [tolerance=±5% resistance=10k package=THT]
  IC1 = MCP23017 I2C I/O Expander
  IC2 = MCP23017 I2C I/O Expander
  IC3 = MCP23017 I2C I/O Expander
  R3 = Resistor [tolerance=±5% resistance=10k package=THT]
  R4 = Resistor [tolerance=±5% resistance=10k package=THT]
  IC4 = MCP23017 I2C I/O Expander
  IC5 = MCP23017 I2C I/O Expander

nets:
  N1: R1.Pin_0, IC1.RESET
  VSS: R1.Pin_1, R2.Pin_1, IC1.VSS, IC2.VDD, IC2.RESET
  N2: R2.Pin_0, IC2.INTB
  N3: IC1.NC#11, IC1.A0, IC2.VSS, IC2.A1, IC3.GPB0
  N4: IC1.SCL, IC2.NC#11
  N5: IC1.SDA, IC2.SCL, IC2.NC#14, IC2.A0
  N6: IC3.GPA7, IC4.NC#11, IC4.A0, IC5.VSS, IC5.A1
  N7: R3.Pin_0, IC5.INTB
  VSS_2: R3.Pin_1, R4.Pin_1, IC4.VSS, IC5.VDD, IC5.RESET
  N8: R4.Pin_0, IC4.RESET
  N9: IC4.SCL, IC5.NC#11
  N10: IC4.SDA, IC5.SCL, IC5.NC#14, IC5.A0

custom parts:
  MCP23017 I2C I/O Expander: The MCP23017 uses two i2c pins (these can be shared with other i2c devices), and in exchange gives you 16 general purpose pins. You can set each of 16 pins to be input, output, input with a pullup or open drain. There's even the ability to get an interrupt via an external pin when any of the inputs change so you don't have to keep polling the chip.
