# Fritzing sketch mcp23017_wiring (saved by Fritzing 0.9.3b)
breadboards: 1

parts:
  IC1 = MCP23017 I2C I/O Expander
  R1 = Resistor [tolerance=±5% resistance=10k package=THT]

nets:
  N1: IC1.VSS, IC1.A0, R1.Pin_1
  N2: IC1.RESET, R1.Pin_0

custom parts:
  MCP23017 I2C I/O Expander: The MCP23017 uses two i2c pins (these can be shared with other i2c devices), and in exchange gives you 16 general purpose pins. You can set each of 16 pins to be input, output, input with a pullup or open drain. There's even the ability to get an interrupt via an external pin when any of the inputs change so you don't have to keep polling the chip.
